# Fritzing sketch Smart Room (saved by Fritzing 0.9.4)
breadboards: 1

parts:
  Teensy_3_1 = Teensy 3.1
  Part1 = 12 NeoPixel Ring [part_number=1643]
  OLED_I2C1 = OLED 128x64 I2C Monochrome Display
  M1 = BMP280
  S1 = Pushbutton [package="[THT]"]
  Mod1 = KY-026 Flame Sensor Module [package="Breakout board"]
  R1 = Resistor [tolerance=±5% resistance=220 package=THT]
  WIZ820io1 = WIZ820io [part_number=WIZ820io]

nets (from the breadboard view):
  N1: Teensy_3_1.D13, WIZ820io1.SCLK
  N2: Teensy_3_1.A1/D15, Part1.IN
  N3: Teensy_3_1.A2/D16, M1.SDA
  N4: Teensy_3_1.A3/D17, M1.SCL
  N5: Teensy_3_1.A4/D18, OLED_I2C1.SDA
  N6: Teensy_3_1.A5/D19, OLED_I2C1.SCK
  N7: Teensy_3_1.A6/D20, Mod1.D0
  N8: Teensy_3_1.A7/D21, Mod1.A0
  N9: Teensy_3_1.A9/D23, S1.Pin_1, S1.Pin_2, R1.Pin_0
  VDD: Part1.VDD, OLED_I2C1.VDD, M1.VIN, S1.Pin_3, S1.Pin_4, Mod1.+, WIZ820io1.VIN
  GND: Part1.GND, OLED_I2C1.GND, M1.GND, Mod1.G, R1.Pin_1, WIZ820io1.GND

custom parts:
  12 NeoPixel Ring: 12 ultra bright smart LED NeoPixels are arranged in a circle with 1.5" (37mm) outer diameter. The rings are 'chainable' - connect the output pin of one to the input pin of another. Use only one microcontroller pin to control as many as you can chain together! Each LED is addressable as the driver chip is inside the LED. Each one has ~18mA constant current drive so the color will be very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
  BMP280: Temperature Humidity Barometric presure Sensor, I2C
  Pushbutton: A generic pushbutton.
  KY-026 Flame Sensor Module: KY-026 Flame Sensor Module reacts in the presence of fire.
